# Fritzing sketch Test (saved by Fritzing 1.0.2b)
breadboards: 1

parts:
  TestGen_Meadow = Meadow F7 Micro
  Main_Meadow = Meadow F7 Micro
  S1 = Momentary Switch [package=ksa_sealed_tac_switch]
  R1 = Resistor [tolerance=±5% resistance=4.7k package="0402 [SMD]"]
  R2 = Resistor [tolerance=±5% resistance=4.7k package="0402 [SMD]"]
  SC16IS752_Breakout = Breakout for SC16IS752 UART and GPIO extender [package=2x5-ra]
  R3 = Resistor [tolerance=±5% resistance=1k package="0402 [SMD]"]

nets:
  3.3V: TestGen_Meadow.3.3V, Main_Meadow.3.3V, S1.1, R1.Pin_0, R2.Pin_0, SC16IS752_Breakout.VCC, SC16IS752_Breakout.A0/CS, SC16IS752_Breakout.A1/SI, R3.Pin_1
  GND: TestGen_Meadow.GND, Main_Meadow.GND, SC16IS752_Breakout.GND
  N1: TestGen_Meadow.DO0, S1.3
  N2: TestGen_Meadow.D12, SC16IS752_Breakout.RxA
  N3: TestGen_Meadow.D13, SC16IS752_Breakout.TxA
  +5V: TestGen_Meadow.+5V, Main_Meadow.+5V
  N4: Main_Meadow.DO0, SC16IS752_Breakout.IRQ, R3.Pin_0
  N5: Main_Meadow.DO7, R1.Pin_1, SC16IS752_Breakout.SDA/VSS
  N6: Main_Meadow.DO8, R2.Pin_1, SC16IS752_Breakout.SCL/SCLK
  N7: SC16IS752_Breakout.GP7, SC16IS752_Breakout.GP3
  N8: SC16IS752_Breakout.GP6, SC16IS752_Breakout.GP2
  N9: SC16IS752_Breakout.GP5, SC16IS752_Breakout.GP1
  N10: SC16IS752_Breakout.GP4, SC16IS752_Breakout.GP0

notes:
  Main Meadow connected to SC16IS752.
  Getting UART messages via I2C (D07&D08)
  Test generator Meadow
  Sending serial messages from COM1 (D12&D13)
  Meadow to generate serial messages on COM1 (D12&D13)
  Meadow connected to SC16IS752 over I2C (D07&D08). Receiving long messages from UART on SC16IS752.

custom parts:
  Breakout for SC16IS752 UART and GPIO extender: Breakout board for SC16IS752.
